// Logisim project Mips_procesor.circ as structural Verilog: 7 circuits, main circuit main
module main (
  input  Clock,
  input  Reset
);

  wire maincontrol_1_alusrc, maincontrol_1_beq, maincontrol_1_bne, maincontrol_1_j, maincontrol_1_jr_2,
       maincontrol_1_memread, maincontrol_1_memtoreg, maincontrol_1_memwrite, maincontrol_1_rd,
       maincontrol_1_rw, nextpc_1_out_7;
  wire [3:0] alucontrol_1_izlazi, alucontrol_1_izlazr, multiplexer_5_out;
  wire [4:0] multiplexer_3_out, multiplexer_4_out;
  wire [5:0] mipsprogramrom_1_p1_2;
  wire [25:0] mipsprogramrom_1_p1;
  wire [29:0] multiplexer_1_out, nextpc_1_out_8;
  wire [31:0] bit_extender_1_out, mips_alu_1_p5, mips_ram_1_p4, multiplexer_2_out, multiplexer_6_out,
       multiplexer_8_out, register_1_q_2, registerfile_1_p1, registerfile_1_p7, registerfile_1_p8;
  wire [31:2] register_1_q;

  Multiplexer #(.width(30)) multiplexer_1 (
    .in0(register_1_q_2[31:2]), .in1(nextpc_1_out_8), .out(multiplexer_1_out), .sel(nextpc_1_out_7));  // open: en
  Multiplexer #(.width(32)) multiplexer_2 (
    .in0({multiplexer_1_out, register_1_q_2[1:0]}), .in1(registerfile_1_p7), .out(multiplexer_2_out),
    .sel(maincontrol_1_jr_2));  // open: en
  Register #(.width(32)) register_1 (
    .D(multiplexer_2_out), .Q({register_1_q, register_1_q_2[1:0]}), .clk(Clock), .clr(Reset));  // open: en
  // Incrementer incrementer_1: pin names not known; wires that end beside it: register_1_q, register_1_q_2[31:2], {register_1_q, register_1_q_2[1:0]}
  // MIPSProgramROM mipsprogramrom_1: pin names not known; wires that end beside it: {mipsprogramrom_1_p1_2, mipsprogramrom_1_p1}, {mipsprogramrom_1_p1_2, mipsprogramrom_1_p1}
  MainControl maincontrol_1 (
    .Op5(mipsprogramrom_1_p1_2[5]), .Op4(mipsprogramrom_1_p1_2[4]), .Op3(mipsprogramrom_1_p1_2[3]),
    .Op2(mipsprogramrom_1_p1_2[2]), .Op1(mipsprogramrom_1_p1_2[1]), .Op0(mipsprogramrom_1_p1_2[0]),
    .Jr(mipsprogramrom_1_p1[5:0]), .RD(maincontrol_1_rd), .RW(maincontrol_1_rw),
    .ALUSrc(maincontrol_1_alusrc), .Beq(maincontrol_1_beq), .Bne(maincontrol_1_bne), .J(maincontrol_1_j),
    .MemRead(maincontrol_1_memread), .MemWrite(maincontrol_1_memwrite), .MemToReg(maincontrol_1_memtoreg),
    .Jr_2(maincontrol_1_jr_2));  // open: ExtOp
  Multiplexer #(.width(5)) multiplexer_3 (
    .in0(mipsprogramrom_1_p1[20:16]), .in1(mipsprogramrom_1_p1[15:11]), .out(multiplexer_3_out),
    .sel(maincontrol_1_rd));  // open: en
  Multiplexer #(.width(5)) multiplexer_4 (
    .in0(multiplexer_3_out), .in1({5{1'b1}}), .out(multiplexer_4_out), .sel(maincontrol_1_j));  // open: en
  ALUControl alucontrol_1 (
    .Opcode(mipsprogramrom_1_p1_2), .funct(mipsprogramrom_1_p1[5:0]), .IzlazI(alucontrol_1_izlazi),
    .IzlazR(alucontrol_1_izlazr));
  // RegisterFile registerfile_1: pin names not known; wires that end beside it: registerfile_1_p1, Clock, maincontrol_1_rw, multiplexer_4_out, mipsprogramrom_1_p1[25:21], mipsprogramrom_1_p1[20:16], registerfile_1_p7, registerfile_1_p8
  assign bit_extender_1_out = {{16{1'b0}}, mipsprogramrom_1_p1[15:0]};  // Bit_Extender bit_extender_1
  Multiplexer #(.width(4)) multiplexer_5 (
    .in0(alucontrol_1_izlazr), .in1(alucontrol_1_izlazi), .out(multiplexer_5_out), .sel(maincontrol_1_alusrc));  // open: en
  Multiplexer #(.width(32)) multiplexer_6 (
    .in0(registerfile_1_p8), .in1(bit_extender_1_out), .out(multiplexer_6_out), .sel(maincontrol_1_alusrc));  // open: en
  NextPc nextpc_1 (
    .INCpC(register_1_q_2[31:2]), .Imm26(mipsprogramrom_1_p1), .Zero(mips_alu_1_p5), .out_8(nextpc_1_out_8),
    .out_7(nextpc_1_out_7), .Beq(maincontrol_1_beq), .Bne(maincontrol_1_bne), .J(maincontrol_1_j));
  // Mips_ALU mips_alu_1: pin names not known; wires that end beside it: registerfile_1_p7, multiplexer_6_out, multiplexer_5_out, mipsprogramrom_1_p1[10:6], mips_alu_1_p5, mips_alu_1_p5[23:0], registerfile_1_p8
  Multiplexer #(.width(32)) multiplexer_7 (
    .in0(multiplexer_8_out), .in1(register_1_q_2), .out(registerfile_1_p1), .sel(maincontrol_1_j));  // open: en
  // MIPS_RAM mips_ram_1: pin names not known; wires that end beside it: maincontrol_1_memwrite, Clock, maincontrol_1_memread, mips_ram_1_p4
  Multiplexer #(.width(32)) multiplexer_8 (
    .in0(mips_alu_1_p5), .in1(mips_ram_1_p4), .out(multiplexer_8_out), .sel(maincontrol_1_memtoreg));  // open: en

  // Notes on the sheet:
  //   Asistentica : Menisa Hrvic
  //   Uradio : Eldar Haseljic
  //   Br. indexa 16116
  //   Profesor : dr.sc Amer Hasanovic
  //   Projekat : Mips procesor (sa Bnq,Bne,J)
endmodule

module Extender (
  input  ExtOp,
  input  [15:0] Ulaz,
  output [31:0] Izlaz
);

  and and_1 (Izlaz[15], ExtOp, Ulaz[15]);

  assign {Izlaz[31:16], Izlaz[14:0]} = {Ulaz, {15{Izlaz[15]}}};
endmodule

// ManiContorl
module MainControl (
  input  Op5,
  input  Op4,
  input  Op3,
  input  Op2,
  input  Op1,
  input  Op0,
  input  [5:0] Jr,
  output RD,
  output RW,
  output ExtOp,
  output ALUSrc,
  output Beq,
  output Bne,
  output J,
  output MemRead,
  output MemWrite,
  output MemToReg,
  output Jr_2
);

  wire and_1_out, and_2_out, and_3_out, and_4_out, and_5_out, and_6_out, and_7_out, and_8_out, and_9_out,
       and_10_out, and_11_out, and_12_out, not_1_out, not_2_out, not_3_out, not_4_out, not_5_out, not_6_out,
       not_7_out, not_8_out, not_9_out, not_10_out, not_11_out, not_12_out, not_13_out, not_14_out,
       not_15_out, not_16_out, not_17_out, not_18_out, not_19_out, not_20_out, not_21_out, not_22_out,
       not_23_out, not_24_out, not_25_out, not_26_out, not_27_out, not_28_out, not_29_out, not_30_out,
       not_31_out, not_32_out;

  and and_1 (and_1_out, ~Op5, ~Op4, ~Op3, ~Op2, ~Op1, ~Op0);  // AND_Gate
  not not_1 (not_1_out, Op5);
  not not_2 (not_2_out, Op4);
  not not_3 (not_3_out, Op3);
  not not_4 (not_4_out, Op2);
  not not_5 (not_5_out, Op4);
  not not_6 (not_6_out, Op3);
  not not_7 (not_7_out, Op2);
  not not_8 (not_8_out, Op4);
  not not_9 (not_9_out, Op3);
  not not_10 (not_10_out, Op2);
  not not_11 (not_11_out, Op2);
  not not_12 (not_12_out, Op1);
  not not_13 (not_13_out, Op2);
  not not_14 (not_14_out, Op0);
  not not_15 (not_15_out, Op2);
  not not_16 (not_16_out, Op5);
  not not_17 (not_17_out, Op3);
  not not_18 (not_18_out, Op0);
  not not_19 (not_19_out, Op5);
  not not_20 (not_20_out, Op3);
  not not_21 (not_21_out, Op1);
  not not_22 (not_22_out, Op5);
  not not_23 (not_23_out, Op3);
  not not_24 (not_24_out, Op3);
  and and_2 (and_2_out, ~Jr[0], ~Jr[1], ~Jr[2], Jr[3], ~Jr[4], ~Jr[5]);  // AND_Gate
  not not_25 (not_25_out, Op5);
  and and_3 (and_3_out, not_25_out, not_26_out, not_27_out);
  not not_26 (not_26_out, Op3);
  not not_27 (not_27_out, Op0);
  and and_4 (and_4_out, not_1_out, not_2_out, not_3_out, not_4_out, Op1);
  not not_28 (not_28_out, Op3);
  and and_5 (and_5_out, not_28_out, not_29_out, not_30_out);
  not not_29 (not_29_out, Op2);
  not not_30 (not_30_out, Op1);
  and and_6 (and_6_out, not_5_out, not_6_out, not_7_out, Op0);
  not not_31 (not_31_out, Op5);
  and and_7 (and_7_out, not_31_out, Op3);
  and and_8 (and_8_out, Op5, not_32_out);
  not not_32 (not_32_out, Op3);
  and and_9 (and_9_out, not_8_out, not_9_out, not_10_out);
  and and_10 (and_10_out, not_11_out, not_12_out);
  and and_11 (and_11_out, not_13_out, not_14_out);
  and and_12 (and_12_out, Op5, not_15_out);
  or or_1 (ALUSrc, Op3, Op5);
  and and_13 (Beq, not_16_out, not_17_out, Op2, not_18_out);
  and and_14 (Bne, not_19_out, not_20_out, not_21_out, Op0);
  and and_15 (J, not_22_out, not_23_out, Op1);
  and and_16 (MemRead, Op5, not_24_out);
  and and_17 (MemWrite, Op5, Op3);
  or or_2 (RD, and_3_out, and_4_out);
  or or_3 (RW, and_5_out, and_6_out, and_7_out, and_8_out);
  or or_4 (ExtOp, and_9_out, and_10_out, and_11_out, and_12_out);
  and and_18 (Jr_2, and_1_out, and_2_out);

  assign MemToReg = Op5;
endmodule

// CTR
module ALUControl (
  input  [5:0] Opcode,
  input  [5:0] funct,
  output [3:0] IzlazI,
  output [3:0] IzlazR
);

  AluCtrI aluctri_1 (
    .O6(Opcode[5]), .O5(Opcode[4]), .O4(Opcode[3]), .O3(Opcode[2]), .O2(Opcode[1]), .O1(Opcode[0]),
    .A4(IzlazI[0]), .A3(IzlazI[1]), .A2(IzlazI[2]), .A1(IzlazI[3]));
  AluCtrR aluctrr_1 (
    .F6(funct[5]), .F5(funct[4]), .F4(funct[3]), .F3(funct[2]), .F2(funct[1]), .F1(funct[0]), .A4(IzlazR[3]),
    .A3(IzlazR[2]), .A2(IzlazR[1]), .A1(IzlazR[0]));
endmodule

module AluCtrR (
  input  F6,
  input  F5,
  input  F4,
  input  F3,
  input  F2,
  input  F1,
  output A4,
  output A3,
  output A2,
  output A1
);


  assign A1 = 1'b0;
  assign A2 = F1;
  assign A3 = F2;
  assign A4 = F3;
endmodule

// AluCtrl
module AluCtrI (
  input  O6,
  input  O5,
  input  O4,
  input  O3,
  input  O2,
  input  O1,
  output A4,
  output A3,
  output A2,
  output A1
);

  wire and_1_out, and_2_out, and_3_out, and_4_out, and_5_out, and_6_out, and_7_out, and_8_out, and_9_out,
       and_10_out, and_11_out, and_12_out, and_13_out, and_14_out, and_15_out, and_16_out, and_17_out,
       and_18_out, and_19_out, and_20_out, and_21_out, not_1_out, not_2_out, not_3_out, not_4_out, not_5_out,
       not_6_out, not_7_out, not_8_out, not_9_out, not_10_out, not_11_out, not_12_out, not_13_out,
       not_14_out, not_15_out, not_16_out, not_17_out, not_18_out, not_19_out, not_20_out, not_21_out,
       not_22_out, not_23_out, not_24_out, not_25_out, not_26_out, not_27_out, not_28_out;

  not not_1 (not_1_out, O6);
  not not_2 (not_2_out, O5);
  not not_3 (not_3_out, O3);
  not not_4 (not_4_out, O1);
  not not_5 (not_5_out, O4);
  not not_6 (not_6_out, O1);
  not not_7 (not_7_out, O4);
  not not_8 (not_8_out, O1);
  not not_9 (not_9_out, O6);
  not not_10 (not_10_out, O5);
  not not_11 (not_11_out, O2);
  not not_12 (not_12_out, O1);
  not not_13 (not_13_out, O4);
  not not_14 (not_14_out, O5);
  not not_15 (not_15_out, O3);
  not not_16 (not_16_out, O4);
  not not_17 (not_17_out, O4);
  not not_18 (not_18_out, O2);
  not not_19 (not_19_out, O6);
  not not_20 (not_20_out, O1);
  not not_21 (not_21_out, O4);
  not not_22 (not_22_out, O3);
  not not_23 (not_23_out, O2);
  not not_24 (not_24_out, O3);
  not not_25 (not_25_out, O2);
  not not_26 (not_26_out, O6);
  not not_27 (not_27_out, O5);
  not not_28 (not_28_out, O2);
  and and_1 (and_1_out, not_1_out, not_2_out, O4, not_3_out, O2, not_4_out);
  and and_2 (and_2_out, O4, O3, O2, O1);
  and and_3 (and_3_out, O5, O4, O3);
  and and_4 (and_4_out, O6, O4, O3);
  and and_5 (and_5_out, not_5_out, O2, not_6_out);
  and and_6 (and_6_out, not_7_out, O3, O2);
  and and_7 (and_7_out, O3, O2, not_8_out);
  and and_8 (and_8_out, not_9_out, not_10_out, O4, not_11_out);
  and and_9 (and_9_out, O5, O2, not_12_out);
  and and_10 (and_10_out, O5, not_13_out, O3);
  and and_11 (and_11_out, O6, not_14_out, not_15_out, O2);
  and and_12 (and_12_out, O6, not_16_out, O3);
  and and_13 (and_13_out, not_17_out, not_18_out, O1);
  and and_14 (and_14_out, not_19_out, O2);
  and and_15 (and_15_out, O2, not_20_out);
  and and_16 (and_16_out, not_21_out, O3);
  and and_17 (and_17_out, O3, O2);
  and and_18 (and_18_out, O5, O1);
  and and_19 (and_19_out, O5, O4, not_22_out);
  and and_20 (and_20_out, O6, not_23_out, O1);
  and and_21 (and_21_out, O6, O4, not_24_out, not_25_out);
  and and_22 (A1, not_26_out, not_27_out, O4, O3, not_28_out, O1);
  or or_1 (A4, and_1_out, and_2_out, and_3_out, and_4_out);
  or or_2 (A3, and_5_out, and_6_out, and_7_out, and_8_out, and_9_out, and_10_out, and_11_out, and_12_out);
  or or_3 (A2, and_13_out, and_14_out, and_15_out, and_16_out, and_17_out, and_18_out, and_19_out, and_20_out, and_21_out);
endmodule

// Next
module NextPc (
  input  [29:0] INCpC,
  input  [25:0] Imm26,
  input  Beq,
  input  Bne,
  input  [31:0] Zero,
  input  J,
  output out_7,
  output [29:0] out_8
);

  wire and_1_out, and_2_out;
  wire [29:0] adder_1_out, bit_extender_1_out;
  wire [31:0] xor_1_out;

  assign bit_extender_1_out = {{14{1'b0}}, Imm26[15:0]};  // Bit_Extender bit_extender_1
  Adder #(.width(30)) adder_1 (.a(INCpC), .b(bit_extender_1_out), .out(adder_1_out));  // open: cin, cout
  Multiplexer #(.width(30)) multiplexer_1 (
    .in0(adder_1_out), .in1({INCpC[29:26], Imm26}), .out(out_8), .sel(J));  // open: en
  assign xor_1_out = Zero ^ {32{1'b0}};  // XOR_Gate xor_1, 32 bits wide
  or or_1 (out_7, and_1_out, J, and_2_out);
  and and_1 (and_1_out, ~xor_1_out[0], Bne);  // AND_Gate
  and and_2 (and_2_out, xor_1_out[0], Beq);
endmodule
